# Fritzing sketch fingerprint_RFID (saved by Fritzing 0.9.0b)

parts:
  부품3 = sensor_biometrico
  KY-1 = Keyes Relay [package=THT]
  부품4 = RFID-RC522-v3
  M1 = DC Motor
  A1 = WeMos D1 R1

nets:
  VCC: 부품3.VCC, 부품4.3.3V, A1.Pin_7
  N1: 부품3.TX, A1.Pin_50
  N2: 부품3.RX, A1.Pin_44, A1.Pin_72
  GND: 부품3.GND, KY-1.power, 부품4.GND, A1.Pin_11, A1.Pin_66
  N3: KY-1.signal, A1.Pin_58
  N4: KY-1.ground, A1.Pin_9
  N5: KY-1.C, M1.pin_1
  N6: KY-1.NO, M1.pin_2
  N7: 부품4.SDA, A1.Pin_25, A1.Pin_46
  N8: 부품4.SCK, A1.Pin_64
  N9: 부품4.MOSI, A1.Pin_60
  N10: 부품4.MISO, A1.Pin_62
  N11: 부품4.RST, A1.Pin_48

custom parts:
  sensor_biometrico: Adafruit Optical Fingerprint Sensor
  Keyes Relay: The Keyes 5V relay module is suitable for SCM development, home appliance control. It uses a 5V~12V TIL control signal which can control DC / AC signal.
  RFID-RC522-v3: A simple China made RFID-RC522 Reader (6x4 cm); do check the pin labels, as this is a MFRC522 based clone.
  WeMos D1 R1: The WeMos D1 is a ESP8266 WiFi based board that uses the Arduino layout with a operating voltage of 3.3V.
